# Fritzing sketch schaltung (saved by Fritzing 0.9.3b)
breadboards: 1

parts:
  U1 = 74HC595 [package="DIP16 [THT]"]
  Raspberry_Pi_B_rev1 = Raspberry Pi B rev1
  R1 = Resistor [tolerance=±5% resistance=220 package=THT]
  R2 = Resistor [tolerance=±5% resistance=220 package=THT]
  LED3 = LED - 3mm [color="Red (633nm)" package="3 mm [THT]"]
  LED4 = LED - 3mm [color="Red (633nm)" package="3 mm [THT]"]

nets:
  N1: U1.Q7, R2.Pin_0
  GND: U1.GND, Raspberry_Pi_B_rev1.GND, LED3.cathode, LED4.cathode
  N2: U1.SH_CP, Raspberry_Pi_B_rev1.GPIO_17
  N3: U1.ST_CP, Raspberry_Pi_B_rev1.GPIO_18
  N4: U1.OE, Raspberry_Pi_B_rev1.GPIO_21
  N5: U1.DS, Raspberry_Pi_B_rev1.GPIO_4
  N6: U1.Q0, R1.Pin_0
  VCC: U1.VCC, Raspberry_Pi_B_rev1.3V3
  N7: R1.Pin_1, LED3.anode
  N8: R2.Pin_1, LED4.anode
