# Fritzing sketch Sketch (saved by Fritzing 0.9.3b)

parts:
  Raspberry_Pi1 = Raspberry Pi B+
  LPD8806_RGB_LED_Strip1 = LPD8806 RGB LED Strip
  Raspberry_Pi2 = Raspberry Pi B+
  LPD8806_RGB_LED_Strip2 = LPD8806 RGB LED Strip
  J3 = Power Jack [package=power_jack_pth]

nets:
  N1: Raspberry_Pi1.GPIO9, LPD8806_RGB_LED_Strip1.DI
  GND: Raspberry_Pi1.GND, LPD8806_RGB_LED_Strip1.GND, LPD8806_RGB_LED_Strip1.CI
  5V: Raspberry_Pi1.5V, LPD8806_RGB_LED_Strip1.+5V
  N2: Raspberry_Pi2.GPIO9, LPD8806_RGB_LED_Strip2.DI
  GND_2: Raspberry_Pi2.GND, LPD8806_RGB_LED_Strip2.GND, LPD8806_RGB_LED_Strip2.CI
  N3: LPD8806_RGB_LED_Strip2.+5V, J3.PWR

custom parts:
  LPD8806 RGB LED Strip: Digitally addressable RGB LED strip
