# Fritzing sketch schaltung (saved by Fritzing 0.9.3b)
breadboards: 1

parts:
  DS1 = DS18B20 1-Wire Temperature Sensor [part_number=DS18B20]
  Raspberry_Pi1 = Raspberry Pi B rev2
  R1 = Resistor [tolerance=±5% resistance=4.7k package="0603 [SMD]"]

nets:
  GND: DS1.GND, Raspberry_Pi1.GPIO_3, Raspberry_Pi1.GND
  N1: DS1.DQ, Raspberry_Pi1.GPIO_4, R1.Pin_1
  VDD: DS1.VDD, Raspberry_Pi1.3V3, R1.Pin_0
