# Fritzing sketch schaltung (saved by Fritzing 0.9.3b)
breadboards: 1

parts:
  U1 = LCD-16X2 [package=lcd-16x2]
  Raspberry_Pi1 = Raspberry Pi B rev2
  U2 = POT [package=alps_pot]

nets:
  VSS: U1.VSS, U1.R_W, U1.K, Raspberry_Pi1.GND, U2.E
  VDD: U1.VDD, U1.A, Raspberry_Pi1.5V, U2.A
  N1: U1.VO, U2.S
  N2: U1.RS, Raspberry_Pi1.GPIO_25
  N3: U1.E, Raspberry_Pi1.GPIO_10
  N4: U1.DB4, Raspberry_Pi1.GPIO_24
  N5: U1.DB5, Raspberry_Pi1.GPIO_23
  N6: U1.DB6, Raspberry_Pi1.GPIO_18
  N7: U1.DB7, Raspberry_Pi1.GPIO_17
