# Fritzing sketch schaltung (saved by Fritzing 0.9.3b)
circuit board: 8.46667cm x 5.64444cm
breadboards: 1

parts:
  Dot_Matrix1 = LED Dot Matrix 18mm (0.7 INCH)
  R1 = Resistor [tolerance=±5% resistance=220 package=THT]
  R2 = Resistor [tolerance=±5% resistance=220 package=THT]
  Raspberry_Pi_B_rev1 = Raspberry Pi B rev1

nets:
  N1: Dot_Matrix1.Column_1, R1.Pin_1
  N2: Dot_Matrix1.Column_2, R2.Pin_1
  N3: Dot_Matrix1.Row_2, Raspberry_Pi_B_rev1.GPIO_23
  N4: Dot_Matrix1.Row_1, Raspberry_Pi_B_rev1.GPIO_22
  N5: R1.Pin_0, Raspberry_Pi_B_rev1.GPIO_17
  N6: R2.Pin_0, Raspberry_Pi_B_rev1.GPIO_18
