# Fritzing sketch Sketch (saved by Fritzing 0.9.3b)
breadboards: 1

parts:
  Raspberry_Pi_B_rev1 = Raspberry Pi B rev2
  IC1 = IC, DIP package, 14 pins [chip_label=74AHCT125]
  LED_Strip = mystery part, 3 pins [chip_label=?]

nets:
  N1: Raspberry_Pi_B_rev1.5V, IC1.pin14, LED_Strip.pin1
  N2: Raspberry_Pi_B_rev1.GND, IC1.pin1, IC1.pin7, LED_Strip.pin3
  N3: Raspberry_Pi_B_rev1.GPIO_18, IC1.pin2
  N4: IC1.pin3, LED_Strip.pin2
